// Logisim project basic_gates.circ as structural Verilog: 2 circuits, main circuit main
module main (
);

  // AND_Gate and_1 is placed but not wired
  // NAND_Gate nand_1 is placed but not wired
  // OR_Gate or_1 is placed but not wired
  // NOR_Gate nor_1 is placed but not wired
  // XOR_Gate xor_1 is placed but not wired
  T_Flip_Flop t_ff_1 ();  // open: T, clk, Q, Qn, reset, preset
  J_K_Flip_Flop j_k_ff_1 ();  // open: J, K, clk, Q, Qn, preset, reset
  S_R_Flip_Flop s_r_ff_1 ();  // open: S, R, clk, Q, reset, Qn, preset
  D_Flip_Flop d_ff_1 ();  // open: D, clk, Q, Qn, preset, reset
  // NOT_Gate not_1 is placed but not wired
endmodule

module two (
  input  a1,
  input  a2,
  input  in_3,
  input  in_4,
  output out_5,
  output out_6,
  output out_7,
  output out_8
);


  assign out_5 = a1;
  assign out_6 = a2;
  assign out_7 = in_3;
  assign out_8 = in_4;
endmodule
